// Logisim project Circuito logico - Saida G.circ as structural Verilog
module Paridade (
  input  E1,
  input  E2,
  input  E3,
  input  E4,
  input  E5,
  output P
);

  wire and_1_out, and_2_out, and_3_out, and_4_out, and_5_out, and_6_out, and_7_out, and_8_out, and_9_out,
       and_10_out, not_1_out, not_2_out, not_3_out, not_4_out, not_5_out, not_6_out, not_7_out, not_8_out,
       not_9_out, not_10_out, not_11_out, not_12_out, not_13_out, not_14_out, not_15_out, not_16_out,
       not_17_out, not_18_out, not_19_out, not_20_out;

  not not_1 (not_1_out, E1);
  not not_2 (not_2_out, E2);
  not not_3 (not_3_out, E3);
  not not_4 (not_4_out, E4);
  not not_5 (not_5_out, E5);
  not not_6 (not_6_out, E1);
  not not_7 (not_7_out, E2);
  not not_8 (not_8_out, E3);
  not not_9 (not_9_out, E2);
  not not_10 (not_10_out, E4);
  not not_11 (not_11_out, E2);
  not not_12 (not_12_out, E5);
  not not_13 (not_13_out, E3);
  not not_14 (not_14_out, E4);
  not not_15 (not_15_out, E3);
  not not_16 (not_16_out, E5);
  not not_17 (not_17_out, E4);
  not not_18 (not_18_out, E5);
  not not_19 (not_19_out, E4);
  not not_20 (not_20_out, E5);
  and and_1 (and_1_out, not_1_out, not_2_out, not_3_out, not_4_out, not_5_out);
  and and_2 (and_2_out, not_6_out, not_7_out, not_8_out, E4, E5);
  and and_3 (and_3_out, not_9_out, E3, not_10_out, E5);
  and and_4 (and_4_out, not_11_out, E3, E4, not_12_out);
  and and_5 (and_5_out, E2, not_13_out, not_14_out, E5);
  and and_6 (and_6_out, E2, not_15_out, E4, not_16_out);
  and and_7 (and_7_out, E2, E3, not_17_out, not_18_out);
  and and_8 (and_8_out, E2, E3, E4, E5);
  and and_9 (and_9_out, E1, not_19_out, E5);
  and and_10 (and_10_out, E1, E4, not_20_out);
  or or_1 (P, and_1_out, and_2_out, and_3_out, and_4_out, and_5_out, and_6_out, and_7_out, and_8_out, and_9_out, and_10_out);
endmodule

module Saida_A (
  input  E1,
  input  E2,
  input  E3,
  input  E4,
  input  E5,
  output A
);

  wire and_1_out, and_2_out, and_3_out, and_4_out, and_5_out, and_6_out, and_7_out, not_1_out, not_2_out,
       not_3_out, not_4_out, not_5_out, not_6_out, not_7_out, not_8_out, not_9_out, not_10_out, not_11_out,
       not_12_out, not_13_out, not_14_out, not_15_out, not_16_out, not_17_out, not_18_out;

  not not_1 (not_1_out, E1);
  not not_2 (not_2_out, E2);
  not not_3 (not_3_out, E4);
  not not_4 (not_4_out, E5);
  not not_5 (not_5_out, E2);
  not not_6 (not_6_out, E3);
  not not_7 (not_7_out, E4);
  not not_8 (not_8_out, E1);
  not not_9 (not_9_out, E3);
  not not_10 (not_10_out, E1);
  not not_11 (not_11_out, E2);
  not not_12 (not_12_out, E1);
  not not_13 (not_13_out, E5);
  not not_14 (not_14_out, E1);
  not not_15 (not_15_out, E4);
  not not_16 (not_16_out, E2);
  not not_17 (not_17_out, E3);
  not not_18 (not_18_out, E5);
  and and_1 (and_1_out, not_1_out, not_2_out, not_3_out, not_4_out);
  and and_2 (and_2_out, not_5_out, not_6_out, not_7_out, E5);
  and and_3 (and_3_out, not_8_out, not_9_out, E4, E5);
  and and_4 (and_4_out, not_10_out, not_11_out, E3, E4);
  and and_5 (and_5_out, not_12_out, E3, E4, not_13_out);
  and and_6 (and_6_out, not_14_out, E2, E3, not_15_out, E5);
  and and_7 (and_7_out, E1, not_16_out, not_17_out, E4, not_18_out);
  or or_1 (A, and_1_out, and_2_out, and_3_out, and_4_out, and_5_out, and_6_out, and_7_out);
endmodule

module Saida_B (
  input  E1,
  input  E2,
  input  E3,
  input  E4,
  input  E5,
  output B
);

  wire and_1_out, and_2_out, and_3_out, and_4_out, and_5_out, not_1_out, not_2_out, not_3_out, not_4_out,
       not_5_out, not_6_out, not_7_out, not_8_out, not_9_out, not_10_out;

  not not_1 (not_1_out, E2);
  not not_2 (not_2_out, E3);
  not not_3 (not_3_out, E4);
  not not_4 (not_4_out, E1);
  not not_5 (not_5_out, E5);
  not not_6 (not_6_out, E1);
  not not_7 (not_7_out, E5);
  not not_8 (not_8_out, E1);
  not not_9 (not_9_out, E1);
  not not_10 (not_10_out, E3);
  and and_1 (and_1_out, not_1_out, not_2_out, not_3_out, E5);
  and and_2 (and_2_out, not_4_out, E4, not_5_out);
  and and_3 (and_3_out, not_6_out, E3, not_7_out);
  and and_4 (and_4_out, not_8_out, E3, E4);
  and and_5 (and_5_out, not_9_out, E2, not_10_out);
  or or_1 (B, and_1_out, and_2_out, and_3_out, and_4_out, and_5_out);
endmodule

module Saida_C (
  input  E1,
  input  E2,
  input  E3,
  input  E4,
  input  E5,
  output C
);

  wire and_1_out, and_2_out, and_3_out, and_4_out, and_5_out, not_1_out, not_2_out, not_3_out, not_4_out,
       not_5_out, not_6_out, not_7_out, not_8_out, not_9_out, not_10_out, not_11_out, not_12_out, not_13_out,
       not_14_out;

  not not_1 (not_1_out, E1);
  not not_2 (not_2_out, E2);
  not not_3 (not_3_out, E3);
  not not_4 (not_4_out, E1);
  not not_5 (not_5_out, E2);
  not not_6 (not_6_out, E4);
  not not_7 (not_7_out, E1);
  not not_8 (not_8_out, E3);
  not not_9 (not_9_out, E4);
  not not_10 (not_10_out, E1);
  not not_11 (not_11_out, E5);
  not not_12 (not_12_out, E2);
  not not_13 (not_13_out, E3);
  not not_14 (not_14_out, E4);
  and and_1 (and_1_out, not_1_out, not_2_out, not_3_out);
  and and_2 (and_2_out, not_4_out, not_5_out, not_6_out);
  and and_3 (and_3_out, not_7_out, not_8_out, not_9_out);
  and and_4 (and_4_out, not_10_out, not_11_out);
  and and_5 (and_5_out, not_12_out, not_13_out, not_14_out, E5);
  or or_1 (C, and_1_out, and_2_out, and_3_out, and_4_out, and_5_out);
endmodule

module Saida_D (
  input  E1,
  input  E2,
  input  E3,
  input  E4,
  input  E5,
  output D
);

  wire and_1_out, and_2_out, and_3_out, and_4_out, and_5_out, and_6_out, not_1_out, not_2_out, not_3_out,
       not_4_out, not_5_out, not_6_out, not_7_out, not_8_out, not_9_out, not_10_out, not_11_out, not_12_out,
       not_13_out, not_14_out, not_15_out;

  not not_1 (not_1_out, E2);
  not not_2 (not_2_out, E3);
  not not_3 (not_3_out, E4);
  not not_4 (not_4_out, E5);
  not not_5 (not_5_out, E1);
  not not_6 (not_6_out, E2);
  not not_7 (not_7_out, E4);
  not not_8 (not_8_out, E1);
  not not_9 (not_9_out, E2);
  not not_10 (not_10_out, E5);
  not not_11 (not_11_out, E1);
  not not_12 (not_12_out, E3);
  not not_13 (not_13_out, E1);
  not not_14 (not_14_out, E2);
  not not_15 (not_15_out, E3);
  and and_1 (and_1_out, not_1_out, not_2_out, not_3_out, not_4_out);
  and and_2 (and_2_out, not_5_out, not_6_out, E3, not_7_out);
  and and_3 (and_3_out, not_8_out, not_9_out, E3, not_10_out);
  and and_4 (and_4_out, not_11_out, E2, not_12_out, E4);
  and and_5 (and_5_out, not_13_out, E2, E4, E5);
  and and_6 (and_6_out, E1, not_14_out, not_15_out);
  or or_1 (D, and_1_out, and_2_out, and_3_out, and_4_out, and_5_out, and_6_out);
endmodule

module Saida_E (
  input  E1,
  input  E2,
  input  E3,
  input  E4,
  input  E5,
  output E
);

  wire and_1_out, and_2_out, and_3_out, and_4_out, and_5_out, and_6_out, not_1_out, not_2_out, not_3_out,
       not_4_out, not_5_out, not_6_out, not_7_out, not_8_out, not_9_out, not_10_out, not_11_out, not_12_out,
       not_13_out, not_14_out;

  not not_1 (not_1_out, E1);
  not not_2 (not_2_out, E2);
  not not_3 (not_3_out, E1);
  not not_4 (not_4_out, E2);
  not not_5 (not_5_out, E1);
  not not_6 (not_6_out, E3);
  not not_7 (not_7_out, E5);
  not not_8 (not_8_out, E1);
  not not_9 (not_9_out, E4);
  not not_10 (not_10_out, E2);
  not not_11 (not_11_out, E3);
  not not_12 (not_12_out, E5);
  not not_13 (not_13_out, E2);
  not not_14 (not_14_out, E3);
  and and_1 (and_1_out, not_1_out, not_2_out, E5);
  and and_2 (and_2_out, not_3_out, not_4_out, E3, E4);
  and and_3 (and_3_out, not_5_out, E2, not_6_out, not_7_out);
  and and_4 (and_4_out, not_8_out, E2, E3, not_9_out);
  and and_5 (and_5_out, E1, not_10_out, not_11_out, not_12_out);
  and and_6 (and_6_out, E1, not_13_out, not_14_out, E4);
  or or_1 (E, and_1_out, and_2_out, and_3_out, and_4_out, and_5_out, and_6_out);
endmodule

module Saida_F (
  input  E1,
  input  E2,
  input  E3,
  input  E4,
  input  E5,
  output F
);

  wire and_1_out, and_2_out, and_3_out, and_4_out, and_5_out, and_6_out, and_7_out, not_1_out, not_2_out,
       not_3_out, not_4_out, not_5_out, not_6_out, not_7_out, not_8_out, not_9_out, not_10_out, not_11_out,
       not_12_out, not_13_out, not_14_out, not_15_out, not_16_out, not_17_out;

  not not_1 (not_1_out, E1);
  not not_2 (not_2_out, E2);
  not not_3 (not_3_out, E3);
  not not_4 (not_4_out, E4);
  not not_5 (not_5_out, E1);
  not not_6 (not_6_out, E4);
  not not_7 (not_7_out, E5);
  not not_8 (not_8_out, E2);
  not not_9 (not_9_out, E3);
  not not_10 (not_10_out, E5);
  not not_11 (not_11_out, E1);
  not not_12 (not_12_out, E2);
  not not_13 (not_13_out, E1);
  not not_14 (not_14_out, E1);
  not not_15 (not_15_out, E4);
  not not_16 (not_16_out, E2);
  not not_17 (not_17_out, E3);
  and and_1 (and_1_out, not_1_out, not_2_out, not_3_out, not_4_out);
  and and_2 (and_2_out, not_5_out, not_6_out, not_7_out);
  and and_3 (and_3_out, not_8_out, not_9_out, not_10_out);
  and and_4 (and_4_out, not_11_out, not_12_out, E3, E4);
  and and_5 (and_5_out, not_13_out, E2, E4, E5);
  and and_6 (and_6_out, not_14_out, E2, E3, not_15_out);
  and and_7 (and_7_out, E1, not_16_out, not_17_out, E4);
  or or_1 (F, and_1_out, and_2_out, and_3_out, and_4_out, and_5_out, and_6_out, and_7_out);
endmodule

module Saida_G (
  input  E1,
  input  E2,
  input  E3,
  input  E4,
  input  E5,
  output G
);

  wire and_1_out, and_2_out, and_3_out, and_4_out, and_5_out, and_6_out, and_7_out, not_1_out, not_2_out,
       not_3_out, not_4_out, not_5_out, not_6_out, not_7_out, not_8_out, not_9_out, not_10_out, not_11_out,
       not_12_out, not_13_out, not_14_out, not_15_out, not_16_out, not_17_out, not_18_out, not_19_out;

  not not_1 (not_1_out, E1);
  not not_2 (not_2_out, E2);
  not not_3 (not_3_out, E3);
  not not_4 (not_4_out, E4);
  not not_5 (not_5_out, E1);
  not not_6 (not_6_out, E2);
  not not_7 (not_7_out, E3);
  not not_8 (not_8_out, E5);
  not not_9 (not_9_out, E1);
  not not_10 (not_10_out, E4);
  not not_11 (not_11_out, E5);
  not not_12 (not_12_out, E1);
  not not_13 (not_13_out, E2);
  not not_14 (not_14_out, E1);
  not not_15 (not_15_out, E3);
  not not_16 (not_16_out, E1);
  not not_17 (not_17_out, E4);
  not not_18 (not_18_out, E2);
  not not_19 (not_19_out, E3);
  and and_1 (and_1_out, not_1_out, not_2_out, not_3_out, not_4_out);
  and and_2 (and_2_out, not_5_out, not_6_out, not_7_out, not_8_out);
  and and_3 (and_3_out, not_9_out, not_10_out, not_11_out);
  and and_4 (and_4_out, not_12_out, not_13_out, E3, E4, E5);
  and and_5 (and_5_out, not_14_out, E2, not_15_out, E4, E5);
  and and_6 (and_6_out, not_16_out, E2, E3, not_17_out);
  and and_7 (and_7_out, E1, not_18_out, not_19_out, E5);
  or or_1 (G, and_1_out, and_2_out, and_3_out, and_4_out, and_5_out, and_6_out, and_7_out);
endmodule
