// Logisim project Projeto completo.circ as structural Verilog: 1 circuit, main circuit main
module main (
  input  E1,
  input  E2,
  input  E3,
  input  E4,
  input  E5,
  input  P,
  output Verifica,
  output A,
  output B,
  output C,
  output D,
  output E,
  output F,
  output G
);

  wire and_1_out, and_2_out, and_3_out, and_4_out, and_5_out, and_6_out, and_7_out, and_8_out, and_9_out,
       and_10_out, and_11_out, and_12_out, and_13_out, and_14_out, and_15_out, and_16_out, and_17_out,
       and_18_out, and_19_out, and_20_out, and_21_out, and_22_out, and_23_out, and_24_out, and_25_out,
       and_26_out, and_27_out, and_28_out, and_29_out, and_30_out, and_31_out, and_32_out, and_33_out,
       and_34_out, and_35_out, and_36_out, and_37_out, and_38_out, and_39_out, and_40_out, and_41_out,
       and_42_out, and_43_out, and_44_out, and_45_out, and_46_out, and_47_out, and_48_out, and_49_out,
       and_50_out, and_51_out, and_52_out, and_53_out, and_54_out, and_55_out, and_56_out, and_57_out,
       and_58_out, and_59_out, and_60_out, and_61_out, and_62_out, and_63_out, and_64_out, and_65_out,
       and_66_out, and_67_out, and_68_out, and_69_out, and_70_out, and_71_out, and_72_out, and_73_out,
       and_74_out, and_75_out, and_76_out, and_77_out, and_78_out, and_79_out, and_80_out, and_81_out,
       and_82_out, and_83_out, and_84_out, and_85_out, and_86_out, and_87_out, and_88_out, and_89_out,
       and_90_out, and_91_out, and_92_out, and_93_out, and_94_out, and_95_out, and_96_out, and_97_out,
       and_98_out, and_99_out, not_1_out, not_2_out, not_3_out, not_4_out, not_5_out, not_6_out, not_7_out,
       not_8_out, not_9_out, not_10_out, not_11_out, not_12_out, not_13_out, not_14_out, not_15_out,
       not_16_out, not_17_out, not_18_out, not_19_out, not_20_out, not_21_out, not_22_out, not_23_out,
       not_24_out, not_25_out, not_26_out, not_27_out, not_28_out, not_29_out, not_30_out, not_31_out,
       not_32_out, not_33_out, not_34_out, not_35_out, not_36_out, not_37_out, not_38_out, not_39_out,
       not_40_out, not_41_out, not_42_out, not_43_out, not_44_out, not_45_out, not_46_out, not_47_out,
       not_48_out, not_49_out, not_50_out, not_51_out, not_52_out, not_53_out, not_54_out, not_55_out,
       not_56_out, not_57_out, not_58_out, not_59_out, not_60_out, not_61_out, not_62_out, not_63_out,
       not_64_out, not_65_out, not_66_out, not_67_out, not_68_out, not_69_out, not_70_out, not_71_out,
       not_72_out, not_73_out, not_74_out, not_75_out, not_76_out, not_77_out, not_78_out, not_79_out,
       not_80_out, not_81_out, not_82_out, not_83_out, not_84_out, not_85_out, not_86_out, not_87_out,
       not_88_out, not_89_out, not_90_out, not_91_out, not_92_out, not_93_out, not_94_out, not_95_out,
       not_96_out, not_97_out, not_98_out, not_99_out, not_100_out, not_101_out, not_102_out, not_103_out,
       not_104_out, not_105_out, not_106_out, not_107_out, not_108_out, not_109_out, not_110_out,
       not_111_out, not_112_out, not_113_out, not_114_out, not_115_out, not_116_out, not_117_out,
       not_118_out, not_119_out, not_120_out, not_121_out, not_122_out, not_123_out, not_124_out,
       not_125_out, not_126_out, not_127_out, not_128_out, not_129_out, not_130_out, not_131_out,
       not_132_out, not_133_out, not_134_out, not_135_out, not_136_out, not_137_out, not_138_out,
       not_139_out, not_140_out, not_141_out, not_142_out, not_143_out, not_144_out, not_145_out,
       not_146_out, not_147_out, not_148_out, not_149_out, not_150_out, not_151_out, not_152_out,
       not_153_out, not_154_out, not_155_out, not_156_out, not_157_out, not_158_out, not_159_out,
       not_160_out, not_161_out, not_162_out, not_163_out, not_164_out, not_165_out, not_166_out,
       not_167_out, not_168_out, not_169_out, not_170_out, not_171_out, not_172_out, not_173_out,
       not_174_out, not_175_out, not_176_out, not_177_out, not_178_out, not_179_out, not_180_out,
       not_181_out, not_182_out, not_183_out, not_184_out, not_185_out, not_186_out, not_187_out,
       not_188_out, not_189_out, not_190_out, not_191_out, not_192_out, not_193_out, not_194_out,
       not_195_out, not_196_out, not_197_out, not_198_out, not_199_out, not_200_out, not_201_out,
       not_202_out, not_203_out, not_204_out, not_205_out, not_206_out, not_207_out, not_208_out,
       not_209_out, not_210_out, not_211_out, not_212_out, not_213_out, not_214_out, not_215_out,
       not_216_out, not_217_out, not_218_out, not_219_out, not_220_out, not_221_out, not_222_out,
       not_223_out, not_224_out, not_225_out, not_226_out, not_227_out, not_228_out, not_229_out,
       not_230_out, not_231_out, not_232_out, not_233_out, not_234_out, not_235_out, not_236_out,
       not_237_out, not_238_out, not_239_out, not_240_out, not_241_out, not_242_out, not_243_out,
       not_244_out, not_245_out, not_246_out, not_247_out, not_248_out, not_249_out, not_250_out,
       not_251_out, not_252_out, not_253_out, not_254_out, not_255_out, not_256_out, not_257_out,
       not_258_out, not_259_out, not_260_out, not_261_out, not_262_out, not_263_out, not_264_out,
       not_265_out, not_266_out, not_267_out, not_268_out, not_269_out, not_270_out, not_271_out,
       not_272_out, not_273_out, not_274_out, not_275_out, not_276_out, not_277_out, not_278_out,
       not_279_out, not_280_out, not_281_out, not_282_out, not_283_out, not_284_out, not_285_out,
       not_286_out, not_287_out, not_288_out, not_289_out, not_290_out, not_291_out;

  not not_1 (not_1_out, E1);
  not not_2 (not_2_out, E2);
  not not_3 (not_3_out, E3);
  not not_4 (not_4_out, E4);
  not not_5 (not_5_out, E5);
  not not_6 (not_6_out, E1);
  not not_7 (not_7_out, E2);
  not not_8 (not_8_out, E3);
  not not_9 (not_9_out, E4);
  not not_10 (not_10_out, P);
  not not_11 (not_11_out, E1);
  not not_12 (not_12_out, E2);
  not not_13 (not_13_out, E3);
  not not_14 (not_14_out, E5);
  not not_15 (not_15_out, P);
  not not_16 (not_16_out, E1);
  not not_17 (not_17_out, E2);
  not not_18 (not_18_out, E3);
  not not_19 (not_19_out, E1);
  not not_20 (not_20_out, E2);
  not not_21 (not_21_out, E4);
  not not_22 (not_22_out, E5);
  not not_23 (not_23_out, P);
  not not_24 (not_24_out, E1);
  not not_25 (not_25_out, E2);
  not not_26 (not_26_out, E4);
  not not_27 (not_27_out, E1);
  not not_28 (not_28_out, E2);
  not not_29 (not_29_out, E5);
  not not_30 (not_30_out, E1);
  not not_31 (not_31_out, E2);
  not not_32 (not_32_out, P);
  not not_33 (not_33_out, E1);
  not not_34 (not_34_out, E3);
  not not_35 (not_35_out, E4);
  not not_36 (not_36_out, E5);
  not not_37 (not_37_out, P);
  not not_38 (not_38_out, E1);
  not not_39 (not_39_out, E3);
  not not_40 (not_40_out, E4);
  not not_41 (not_41_out, E1);
  not not_42 (not_42_out, E3);
  not not_43 (not_43_out, E5);
  not not_44 (not_44_out, E1);
  not not_45 (not_45_out, E3);
  not not_46 (not_46_out, P);
  not not_47 (not_47_out, E1);
  not not_48 (not_48_out, E4);
  not not_49 (not_49_out, E5);
  not not_50 (not_50_out, E1);
  not not_51 (not_51_out, E4);
  not not_52 (not_52_out, P);
  not not_53 (not_53_out, E1);
  not not_54 (not_54_out, E5);
  not not_55 (not_55_out, P);
  not not_56 (not_56_out, E1);
  not not_57 (not_57_out, E2);
  not not_58 (not_58_out, E3);
  not not_59 (not_59_out, E4);
  not not_60 (not_60_out, E5);
  not not_61 (not_61_out, P);
  not not_62 (not_62_out, E2);
  not not_63 (not_63_out, E3);
  not not_64 (not_64_out, E4);
  not not_65 (not_65_out, E2);
  not not_66 (not_66_out, E3);
  not not_67 (not_67_out, E5);
  not not_68 (not_68_out, E2);
  not not_69 (not_69_out, E3);
  not not_70 (not_70_out, P);
  not not_71 (not_71_out, E1);
  not not_72 (not_72_out, E2);
  not not_73 (not_73_out, E4);
  not not_74 (not_74_out, E5);
  not not_75 (not_75_out, E1);
  not not_76 (not_76_out, E3);
  not not_77 (not_77_out, E4);
  not not_78 (not_78_out, E5);
  not not_79 (not_79_out, E2);
  not not_80 (not_80_out, E3);
  not not_81 (not_81_out, E1);
  not not_82 (not_82_out, P);
  not not_83 (not_83_out, E2);
  not not_84 (not_84_out, E3);
  not not_85 (not_85_out, E4);
  not not_86 (not_86_out, E1);
  not not_87 (not_87_out, E3);
  not not_88 (not_88_out, E1);
  not not_89 (not_89_out, P);
  not not_90 (not_90_out, E1);
  not not_91 (not_91_out, E2);
  not not_92 (not_92_out, E1);
  not not_93 (not_93_out, E5);
  not not_94 (not_94_out, E1);
  not not_95 (not_95_out, P);
  not not_96 (not_96_out, E1);
  not not_97 (not_97_out, E4);
  not not_98 (not_98_out, E2);
  not not_99 (not_99_out, E3);
  not not_100 (not_100_out, E5);
  not not_101 (not_101_out, E1);
  not not_102 (not_102_out, E2);
  not not_103 (not_103_out, E3);
  not not_104 (not_104_out, E4);
  not not_105 (not_105_out, P);
  not not_106 (not_106_out, E1);
  not not_107 (not_107_out, E2);
  not not_108 (not_108_out, E3);
  not not_109 (not_109_out, E5);
  not not_110 (not_110_out, P);
  not not_111 (not_111_out, E1);
  not not_112 (not_112_out, E2);
  not not_113 (not_113_out, E4);
  not not_114 (not_114_out, E5);
  not not_115 (not_115_out, P);
  not not_116 (not_116_out, E1);
  not not_117 (not_117_out, E2);
  not not_118 (not_118_out, E5);
  not not_119 (not_119_out, E1);
  not not_120 (not_120_out, E2);
  not not_121 (not_121_out, P);
  not not_122 (not_122_out, E1);
  not not_123 (not_123_out, E3);
  not not_124 (not_124_out, E4);
  not not_125 (not_125_out, E5);
  not not_126 (not_126_out, P);
  not not_127 (not_127_out, E1);
  not not_128 (not_128_out, E3);
  not not_129 (not_129_out, E4);
  not not_130 (not_130_out, E1);
  not not_131 (not_131_out, E3);
  not not_132 (not_132_out, E5);
  not not_133 (not_133_out, E1);
  not not_134 (not_134_out, E3);
  not not_135 (not_135_out, P);
  not not_136 (not_136_out, E1);
  not not_137 (not_137_out, E4);
  not not_138 (not_138_out, E5);
  not not_139 (not_139_out, E1);
  not not_140 (not_140_out, E5);
  not not_141 (not_141_out, P);
  not not_142 (not_142_out, E1);
  not not_143 (not_143_out, E2);
  not not_144 (not_144_out, E3);
  not not_145 (not_145_out, E4);
  not not_146 (not_146_out, E1);
  not not_147 (not_147_out, E2);
  not not_148 (not_148_out, E4);
  not not_149 (not_149_out, E1);
  not not_150 (not_150_out, E3);
  not not_151 (not_151_out, E1);
  not not_152 (not_152_out, E5);
  not not_153 (not_153_out, E1);
  not not_154 (not_154_out, E2);
  not not_155 (not_155_out, E1);
  not not_156 (not_156_out, E4);
  not not_157 (not_157_out, E2);
  not not_158 (not_158_out, E3);
  not not_159 (not_159_out, E4);
  not not_160 (not_160_out, E2);
  not not_161 (not_161_out, E3);
  not not_162 (not_162_out, E4);
  not not_163 (not_163_out, E2);
  not not_164 (not_164_out, E3);
  not not_165 (not_165_out, E2);
  not not_166 (not_166_out, E3);
  not not_167 (not_167_out, E5);
  not not_168 (not_168_out, P);
  not not_169 (not_169_out, E1);
  not not_170 (not_170_out, P);
  not not_171 (not_171_out, E1);
  not not_172 (not_172_out, E2);
  not not_173 (not_173_out, E3);
  not not_174 (not_174_out, E4);
  not not_175 (not_175_out, E5);
  not not_176 (not_176_out, E1);
  not not_177 (not_177_out, E2);
  not not_178 (not_178_out, E4);
  not not_179 (not_179_out, E5);
  not not_180 (not_180_out, P);
  not not_181 (not_181_out, E1);
  not not_182 (not_182_out, E2);
  not not_183 (not_183_out, E4);
  not not_184 (not_184_out, E1);
  not not_185 (not_185_out, E2);
  not not_186 (not_186_out, E5);
  not not_187 (not_187_out, E1);
  not not_188 (not_188_out, E3);
  not not_189 (not_189_out, E5);
  not not_190 (not_190_out, E1);
  not not_191 (not_191_out, E3);
  not not_192 (not_192_out, P);
  not not_193 (not_193_out, E1);
  not not_194 (not_194_out, E2);
  not not_195 (not_195_out, E3);
  not not_196 (not_196_out, E4);
  not not_197 (not_197_out, E5);
  not not_198 (not_198_out, P);
  not not_199 (not_199_out, E2);
  not not_200 (not_200_out, E3);
  not not_201 (not_201_out, E4);
  not not_202 (not_202_out, E2);
  not not_203 (not_203_out, E3);
  not not_204 (not_204_out, E5);
  not not_205 (not_205_out, E2);
  not not_206 (not_206_out, E3);
  not not_207 (not_207_out, P);
  not not_208 (not_208_out, E1);
  not not_209 (not_209_out, E3);
  not not_210 (not_210_out, E4);
  not not_211 (not_211_out, P);
  not not_212 (not_212_out, E2);
  not not_213 (not_213_out, E3);
  not not_214 (not_214_out, E4);
  not not_215 (not_215_out, P);
  not not_216 (not_216_out, E1);
  not not_217 (not_217_out, E2);
  not not_218 (not_218_out, E1);
  not not_219 (not_219_out, E3);
  not not_220 (not_220_out, E1);
  not not_221 (not_221_out, E5);
  not not_222 (not_222_out, E1);
  not not_223 (not_223_out, P);
  not not_224 (not_224_out, E1);
  not not_225 (not_225_out, E2);
  not not_226 (not_226_out, E1);
  not not_227 (not_227_out, E3);
  not not_228 (not_228_out, E5);
  not not_229 (not_229_out, E1);
  not not_230 (not_230_out, E4);
  not not_231 (not_231_out, E2);
  not not_232 (not_232_out, E3);
  not not_233 (not_233_out, E5);
  not not_234 (not_234_out, E2);
  not not_235 (not_235_out, E3);
  not not_236 (not_236_out, E1);
  not not_237 (not_237_out, E2);
  not not_238 (not_238_out, E3);
  not not_239 (not_239_out, E4);
  not not_240 (not_240_out, E1);
  not not_241 (not_241_out, E3);
  not not_242 (not_242_out, P);
  not not_243 (not_243_out, E1);
  not not_244 (not_244_out, E4);
  not not_245 (not_245_out, E5);
  not not_246 (not_246_out, E1);
  not not_247 (not_247_out, E4);
  not not_248 (not_248_out, P);
  not not_249 (not_249_out, E2);
  not not_250 (not_250_out, E3);
  not not_251 (not_251_out, E5);
  not not_252 (not_252_out, E2);
  not not_253 (not_253_out, E3);
  not not_254 (not_254_out, P);
  not not_255 (not_255_out, E1);
  not not_256 (not_256_out, E2);
  not not_257 (not_257_out, E1);
  not not_258 (not_258_out, E1);
  not not_259 (not_259_out, E2);
  not not_260 (not_260_out, E3);
  not not_261 (not_261_out, E1);
  not not_262 (not_262_out, E2);
  not not_263 (not_263_out, E3);
  not not_264 (not_264_out, E5);
  not not_265 (not_265_out, E1);
  not not_266 (not_266_out, E2);
  not not_267 (not_267_out, P);
  not not_268 (not_268_out, E1);
  not not_269 (not_269_out, E3);
  not not_270 (not_270_out, P);
  not not_271 (not_271_out, E1);
  not not_272 (not_272_out, E4);
  not not_273 (not_273_out, E5);
  not not_274 (not_274_out, E2);
  not not_275 (not_275_out, E3);
  not not_276 (not_276_out, E4);
  not not_277 (not_277_out, E1);
  not not_278 (not_278_out, P);
  not not_279 (not_279_out, E2);
  not not_280 (not_280_out, E3);
  not not_281 (not_281_out, P);
  not not_282 (not_282_out, E1);
  not not_283 (not_283_out, E2);
  not not_284 (not_284_out, E1);
  not not_285 (not_285_out, E3);
  not not_286 (not_286_out, E1);
  not not_287 (not_287_out, E4);
  not not_288 (not_288_out, E1);
  not not_289 (not_289_out, E5);
  not not_290 (not_290_out, E2);
  not not_291 (not_291_out, E3);
  and and_1 (and_1_out, not_1_out, not_2_out, not_3_out, not_4_out, not_5_out, P);
  and and_2 (and_2_out, not_6_out, not_7_out, not_8_out, not_9_out, E5, not_10_out);
  and and_3 (and_3_out, not_11_out, not_12_out, not_13_out, E4, not_14_out, not_15_out);
  and and_4 (and_4_out, not_16_out, not_17_out, not_18_out, E4, E5, P);
  and and_5 (and_5_out, not_19_out, not_20_out, E3, not_21_out, not_22_out, not_23_out);
  and and_6 (and_6_out, not_24_out, not_25_out, E3, not_26_out, E5, P);
  and and_7 (and_7_out, not_27_out, not_28_out, E3, E4, not_29_out, P);
  and and_8 (and_8_out, not_30_out, not_31_out, E3, E4, E5, not_32_out);
  and and_9 (and_9_out, not_33_out, E2, not_34_out, not_35_out, not_36_out, not_37_out);
  and and_10 (and_10_out, not_38_out, E2, not_39_out, not_40_out, E5, P);
  and and_11 (and_11_out, not_41_out, E2, not_42_out, E4, not_43_out, P);
  and and_12 (and_12_out, not_44_out, E2, not_45_out, E4, E5, not_46_out);
  and and_13 (and_13_out, not_47_out, E2, E3, not_48_out, not_49_out, P);
  and and_14 (and_14_out, not_50_out, E2, E3, not_51_out, E5, not_52_out);
  and and_15 (and_15_out, not_53_out, E2, E3, E4, not_54_out, not_55_out);
  and and_16 (and_16_out, not_56_out, E2, E3, E4, E5, P);
  and and_17 (and_17_out, E1, not_57_out, not_58_out, not_59_out, not_60_out, not_61_out);
  and and_18 (and_18_out, E1, not_62_out, not_63_out, not_64_out, E5, P);
  and and_19 (and_19_out, E1, not_65_out, not_66_out, E4, not_67_out, P);
  and and_20 (and_20_out, E1, not_68_out, not_69_out, E4, E5, not_70_out);
  and and_21 (and_21_out, not_71_out, not_72_out, not_73_out, not_74_out);
  and and_22 (and_22_out, not_75_out, not_76_out, not_77_out, not_78_out, P);
  and and_23 (and_23_out, not_79_out, not_80_out, P);
  and and_24 (and_24_out, not_81_out, E5, not_82_out);
  and and_25 (and_25_out, not_83_out, not_84_out, not_85_out, E5);
  and and_26 (and_26_out, not_86_out, not_87_out, E4, E5);
  and and_27 (and_27_out, not_88_out, E3, not_89_out);
  and and_28 (and_28_out, not_90_out, not_91_out, E3, E4);
  and and_29 (and_29_out, not_92_out, E3, E4, not_93_out);
  and and_30 (and_30_out, not_94_out, E2, E4, not_95_out);
  and and_31 (and_31_out, not_96_out, E2, E3, not_97_out, E5);
  and and_32 (and_32_out, E1, not_98_out, not_99_out, E4, not_100_out);
  and and_33 (and_33_out, not_101_out, not_102_out, not_103_out, not_104_out, E5, not_105_out);
  and and_34 (and_34_out, not_106_out, not_107_out, not_108_out, E4, not_109_out, not_110_out);
  and and_35 (and_35_out, not_111_out, not_112_out, E3, not_113_out, not_114_out, not_115_out);
  and and_36 (and_36_out, not_116_out, not_117_out, E3, E4, not_118_out, P);
  and and_37 (and_37_out, not_119_out, not_120_out, E3, E4, E5, not_121_out);
  and and_38 (and_38_out, not_122_out, E2, not_123_out, not_124_out, not_125_out, not_126_out);
  and and_39 (and_39_out, not_127_out, E2, not_128_out, not_129_out, E5, P);
  and and_40 (and_40_out, not_130_out, E2, not_131_out, E4, not_132_out, P);
  and and_41 (and_41_out, not_133_out, E2, not_134_out, E4, E5, not_135_out);
  and and_42 (and_42_out, not_136_out, E2, E3, not_137_out, not_138_out, P);
  and and_43 (and_43_out, not_139_out, E2, E3, E4, not_140_out, not_141_out);
  and and_44 (and_44_out, not_142_out, E2, E3, E4, E5, P);
  and and_45 (and_45_out, E1, not_143_out, not_144_out, not_145_out, E5, P);
  and and_46 (and_46_out, not_146_out, not_147_out, not_148_out);
  and and_47 (and_47_out, not_149_out, not_150_out);
  and and_48 (and_48_out, not_151_out, not_152_out);
  and and_49 (and_49_out, not_153_out, not_154_out, P);
  and and_50 (and_50_out, not_155_out, not_156_out, P);
  and and_51 (and_51_out, not_157_out, not_158_out, not_159_out, P);
  and and_52 (and_52_out, not_160_out, not_161_out, not_162_out, E5);
  and and_53 (and_53_out, not_163_out, not_164_out, E5, P);
  and and_54 (and_54_out, not_165_out, not_166_out, E4, not_167_out, not_168_out);
  and and_55 (and_55_out, not_169_out, E2, E4, not_170_out);
  and and_56 (and_56_out, not_171_out, not_172_out, not_173_out, not_174_out, not_175_out, P);
  and and_57 (and_57_out, not_176_out, not_177_out, E3, not_178_out, not_179_out, not_180_out);
  and and_58 (and_58_out, not_181_out, not_182_out, E3, not_183_out, E5, P);
  and and_59 (and_59_out, not_184_out, not_185_out, E3, E4, not_186_out, P);
  and and_60 (and_60_out, not_187_out, E2, not_188_out, E4, not_189_out, P);
  and and_61 (and_61_out, not_190_out, E2, not_191_out, E4, E5, not_192_out);
  and and_62 (and_62_out, not_193_out, E2, E3, E4, E5, P);
  and and_63 (and_63_out, E1, not_194_out, not_195_out, not_196_out, not_197_out, not_198_out);
  and and_64 (and_64_out, E1, not_199_out, not_200_out, not_201_out, E5, P);
  and and_65 (and_65_out, E1, not_202_out, not_203_out, E4, not_204_out, P);
  and and_66 (and_66_out, E1, not_205_out, not_206_out, E4, E5, not_207_out);
  and and_67 (and_67_out, not_208_out, not_209_out, not_210_out, not_211_out);
  and and_68 (and_68_out, not_212_out, not_213_out, not_214_out, not_215_out);
  and and_69 (and_69_out, not_216_out, not_217_out, E5);
  and and_70 (and_70_out, not_218_out, not_219_out, E4, P);
  and and_71 (and_71_out, not_220_out, E3, not_221_out, P);
  and and_72 (and_72_out, not_222_out, E3, E5, not_223_out);
  and and_73 (and_73_out, not_224_out, not_225_out, E3, E4);
  and and_74 (and_74_out, not_226_out, E2, not_227_out, not_228_out);
  and and_75 (and_75_out, not_229_out, E2, E3, not_230_out);
  and and_76 (and_76_out, E1, not_231_out, not_232_out, not_233_out);
  and and_77 (and_77_out, E1, not_234_out, not_235_out, E4);
  and and_78 (and_78_out, not_236_out, not_237_out, not_238_out, not_239_out);
  and and_79 (and_79_out, not_240_out, not_241_out, not_242_out);
  and and_80 (and_80_out, not_243_out, not_244_out, not_245_out);
  and and_81 (and_81_out, not_246_out, not_247_out, not_248_out);
  and and_82 (and_82_out, not_249_out, not_250_out, not_251_out);
  and and_83 (and_83_out, not_252_out, not_253_out, not_254_out);
  and and_84 (and_84_out, not_255_out, not_256_out, E3, E4);
  and and_85 (and_85_out, not_257_out, E2, E4, E5);
  and and_86 (and_86_out, not_258_out, E2, E3, P);
  and and_87 (and_87_out, E1, not_259_out, not_260_out, E4);
  and and_88 (and_88_out, not_261_out, not_262_out, not_263_out, not_264_out);
  and and_89 (and_89_out, not_265_out, not_266_out, not_267_out);
  and and_90 (and_90_out, not_268_out, not_269_out, not_270_out);
  and and_91 (and_91_out, not_271_out, not_272_out, not_273_out);
  and and_92 (and_92_out, not_274_out, not_275_out, not_276_out, P);
  and and_93 (and_93_out, not_277_out, E5, not_278_out);
  and and_94 (and_94_out, not_279_out, not_280_out, E4, not_281_out);
  and and_95 (and_95_out, not_282_out, not_283_out, E3, E4, E5);
  and and_96 (and_96_out, not_284_out, E2, not_285_out, E4, E5);
  and and_97 (and_97_out, not_286_out, E2, E3, not_287_out);
  and and_98 (and_98_out, not_288_out, E2, E3, not_289_out, P);
  and and_99 (and_99_out, E1, not_290_out, not_291_out, E5);
  or or_1 (C, and_46_out, and_47_out, and_48_out, and_49_out, and_50_out, and_51_out, and_52_out, and_53_out, and_54_out, and_55_out);
  or or_2 (E, and_67_out, and_68_out, and_69_out, and_70_out, and_71_out, and_72_out, and_73_out, and_74_out, and_75_out, and_76_out, and_77_out);
  or or_3 (F, and_78_out, and_79_out, and_80_out, and_81_out, and_82_out, and_83_out, and_84_out, and_85_out, and_86_out, and_87_out);
  or or_4 (Verifica, and_1_out, and_2_out, and_3_out, and_4_out, and_5_out, and_6_out, and_7_out, and_8_out, and_9_out, and_10_out, and_11_out, and_12_out, and_13_out, and_14_out, and_15_out, and_16_out, and_17_out, and_18_out, and_19_out, and_20_out);
  or or_5 (A, and_21_out, and_22_out, and_23_out, and_24_out, and_25_out, and_26_out, and_27_out, and_28_out, and_29_out, and_30_out, and_31_out, and_32_out);
  or or_6 (B, and_33_out, and_34_out, and_35_out, and_36_out, and_37_out, and_38_out, and_39_out, and_40_out, and_41_out, and_42_out, and_43_out, and_44_out, and_45_out);
  or or_7 (D, and_56_out, and_57_out, and_58_out, and_59_out, and_60_out, and_61_out, and_62_out, and_63_out, and_64_out, and_65_out, and_66_out);
  or or_8 (G, and_88_out, and_89_out, and_90_out, and_91_out, and_92_out, and_93_out, and_94_out, and_95_out, and_96_out, and_97_out, and_98_out, and_99_out);
endmodule
